// Logisim project ex4.circ as structural Verilog: 1 circuit, main circuit Split
module Split (
  input  [7:0] In1,
  output Out1,
  output [7:0] Out2
);

  wire not_1_out;

  assign Out2 = {{1{not_1_out}}, In1[6:0]};  // Bit_Extender bit_extender_1
  and and_1 (Out1, In1[0], In1[7]);
  not not_1 (not_1_out, In1[7]);

  // Notes on the sheet:
  //   PUT CIRCUITRY HERE
endmodule
