// Logisim project control-logic.circ as structural Verilog: 1 circuit, main circuit control_logic
module control_logic (
  input  [31:0] Instruction,
  input  BrEq,
  input  BrLt,
  output PCSel,
  output RegWEn,
  output [2:0] ImmSel,
  output BrUn,
  output ASel,
  output BSel,
  output [3:0] ALUSel,
  output MemWEn,
  output [1:0] WBSel
);

  wire and_1_out, and_2_out, and_3_out, and_4_out, and_5_out, and_6_out, and_7_out, and_8_out, and_9_out,
       and_10_out, and_11_out, and_12_out, and_13_out, and_14_out, and_15_out, and_16_out, and_17_out,
       and_18_out, and_19_out, and_20_out, and_21_out, and_22_out, and_23_out, and_24_out, and_25_out,
       and_26_out, and_27_out, and_28_out, and_29_out, and_42_out, and_43_out, and_44_out, and_45_out,
       and_46_out, and_47_out, and_48_out, and_49_out, B_beq, B_bge, B_bgeu, B_blt, B_bltu, B_bne,
       comparator_1_eq, comparator_2_eq, comparator_3_eq, comparator_4_eq, comparator_5_eq, comparator_6_eq,
       comparator_7_eq, comparator_8_eq, comparator_9_eq, comparator_10_eq, comparator_11_eq,
       comparator_12_eq, comparator_13_eq, comparator_14_eq, comparator_15_eq, comparator_16_eq,
       comparator_17_eq, comparator_18_eq, comparator_19_eq, comparator_20_eq, comparator_21_eq,
       comparator_22_eq, comparator_23_eq, comparator_24_eq, comparator_25_eq, comparator_26_eq,
       comparator_27_eq, comparator_28_eq, comparator_29_eq, comparator_30_eq, comparator_31_eq,
       comparator_32_eq, comparator_33_eq, comparator_34_eq, comparator_35_eq, comparator_36_eq,
       comparator_37_eq, comparator_38_eq, comparator_39_eq, comparator_40_eq, comparator_41_eq,
       comparator_42_eq, comparator_43_eq, comparator_44_eq, comparator_45_eq, comparator_46_eq,
       comparator_47_eq, comparator_48_eq, comparator_49_eq, comparator_50_eq, comparator_51_eq,
       comparator_52_eq, comparator_53_eq, comparator_54_eq, not_1_out, not_2_out, not_3_out, or_1_out,
       or_2_out, or_3_out, or_4_out, or_5_out, or_6_out, or_7_out, or_8_out, priority_encoder_4_out,
       priority_encoder_5_out, priority_encoder_6_out, R_add, R_and, R_mul, R_mulh, R_mulhu, R_or, R_sll,
       R_slt, R_sra, R_srl, R_sub, R_xor;
  wire [2:0] priority_encoder_1_out, priority_encoder_2_out;
  wire [3:0] priority_encoder_3_out;
  wire [5:0] B_FORMAT, bit_extender_2_out, bit_extender_3_out, bit_extender_4_out, bit_extender_5_out,
       bit_extender_6_out, bit_extender_7_out, I_FORMAT, Jump, LOAD_FORMAT, multiplexer_1_out, R_FORMAT,
       STORE_FORMAT, U_FORMAT;
  wire [15:14] rom_1_data;

  Comparator #(.mode("unsigned"), .width(7)) comparator_1 (
    .a(Instruction[6:0]), .b(7'b0010011), .eq(comparator_1_eq));  // open: gt, lt
  Comparator #(.mode("unsigned"), .width(7)) comparator_2 (
    .a(Instruction[6:0]), .b(7'b0110011), .eq(comparator_2_eq));  // open: gt, lt
  Comparator #(.mode("unsigned"), .width(7)) comparator_3 (
    .a(Instruction[6:0]), .b(7'b1100011), .eq(comparator_3_eq));  // open: gt, lt
  Comparator #(.mode("unsigned"), .width(7)) comparator_4 (
    .a(Instruction[6:0]), .b(7'b0000011), .eq(comparator_4_eq));  // open: gt, lt
  Comparator #(.mode("unsigned"), .width(7)) comparator_5 (
    .a(Instruction[6:0]), .b(7'b0100011), .eq(comparator_5_eq));  // open: gt, lt
  Comparator #(.mode("unsigned"), .width(7)) comparator_6 (
    .a(Instruction[6:0]), .b(7'b1101111), .eq(comparator_6_eq));  // open: gt, lt
  Comparator #(.mode("unsigned"), .width(7)) comparator_7 (
    .a(Instruction[6:0]), .b(7'b1100111), .eq(comparator_7_eq));  // open: gt, lt
  Comparator #(.mode("unsigned"), .width(7)) comparator_8 (
    .a(Instruction[6:0]), .b(7'b0010111), .eq(comparator_8_eq));  // open: gt, lt
  Comparator #(.mode("unsigned"), .width(7)) comparator_9 (
    .a(Instruction[6:0]), .b(7'b0110111), .eq(comparator_9_eq));  // open: gt, lt
  Multiplexer #(.select(3), .width(6)) multiplexer_1 (
    .in0(I_FORMAT), .in1(R_FORMAT), .in2(B_FORMAT), .in3(LOAD_FORMAT), .in4(STORE_FORMAT), .in5(Jump),
    .in6(U_FORMAT), .out(multiplexer_1_out), .sel(priority_encoder_1_out));  // open: in7
  Priority_Encoder priority_encoder_1 (
    .in0(comparator_1_eq), .in1(comparator_2_eq), .in2(comparator_3_eq), .in3(comparator_4_eq),
    .in4(comparator_5_eq), .in5(or_1_out), .in6(or_2_out), .out(priority_encoder_1_out));  // open: in7, en_in, gs, en_out
  or or_1 (or_1_out, comparator_6_eq, comparator_7_eq);
  or or_2 (or_2_out, comparator_8_eq, comparator_9_eq);
  ROM #(.addrWidth(6), .dataWidth(16)) rom_1 (
    .addr(multiplexer_1_out), .data({rom_1_data, WBSel, MemWEn, ALUSel, BSel, ASel, BrUn, ImmSel, RegWEn}));
  Comparator #(.width(3)) comparator_10 (.a(3'b000), .b(Instruction[14:12]), .eq(comparator_10_eq));  // open: gt, lt
  Comparator #(.width(3)) comparator_11 (.a(3'b001), .b(Instruction[14:12]), .eq(comparator_11_eq));  // open: gt, lt
  Comparator #(.width(3)) comparator_12 (.a(3'b010), .b(Instruction[14:12]), .eq(comparator_12_eq));  // open: gt, lt
  Comparator #(.width(3)) comparator_13 (.a(3'b100), .b(Instruction[14:12]), .eq(comparator_13_eq));  // open: gt, lt
  Comparator #(.width(3)) comparator_14 (.a(3'b101), .b(Instruction[14:12]), .eq(comparator_14_eq));  // open: gt, lt
  Comparator #(.width(3)) comparator_15 (.a(3'b110), .b(Instruction[14:12]), .eq(comparator_15_eq));  // open: gt, lt
  Comparator #(.width(3)) comparator_16 (.a(3'b111), .b(Instruction[14:12]), .eq(comparator_16_eq));  // open: gt, lt
  Comparator #(.mode("unsigned"), .width(7)) comparator_17 (
    .a({7{1'b0}}), .b(Instruction[31:25]), .eq(comparator_17_eq));  // open: gt, lt
  Comparator #(.width(7)) comparator_18 (
    .a(7'b0100000), .b(Instruction[31:25]), .eq(comparator_18_eq));  // open: gt, lt
  Comparator #(.width(3)) comparator_19 (.a(3'b000), .b(Instruction[14:12]), .eq(comparator_19_eq));  // open: gt, lt
  Comparator #(.width(3)) comparator_20 (.a(3'b001), .b(Instruction[14:12]), .eq(comparator_20_eq));  // open: gt, lt
  Comparator #(.width(3)) comparator_21 (.a(3'b010), .b(Instruction[14:12]), .eq(comparator_21_eq));  // open: gt, lt
  Comparator #(.width(3)) comparator_22 (.a(3'b011), .b(Instruction[14:12]), .eq(comparator_22_eq));  // open: gt, lt
  Comparator #(.width(3)) comparator_23 (.a(3'b100), .b(Instruction[14:12]), .eq(comparator_23_eq));  // open: gt, lt
  Comparator #(.width(3)) comparator_24 (.a(3'b101), .b(Instruction[14:12]), .eq(comparator_24_eq));  // open: gt, lt
  Comparator #(.width(3)) comparator_25 (.a(3'b110), .b(Instruction[14:12]), .eq(comparator_25_eq));  // open: gt, lt
  Comparator #(.width(3)) comparator_26 (.a(3'b111), .b(Instruction[14:12]), .eq(comparator_26_eq));  // open: gt, lt
  Comparator #(.mode("unsigned"), .width(7)) comparator_27 (
    .a({7{1'b0}}), .b(Instruction[31:25]), .eq(comparator_27_eq));  // open: gt, lt
  and and_1 (and_1_out, comparator_19_eq, comparator_27_eq);
  and and_2 (and_2_out, comparator_20_eq, comparator_27_eq);
  and and_3 (and_3_out, comparator_21_eq, comparator_27_eq);
  and and_4 (and_4_out, comparator_23_eq, comparator_27_eq);
  and and_5 (and_5_out, comparator_24_eq, comparator_27_eq);
  and and_6 (and_6_out, comparator_25_eq, comparator_27_eq);
  and and_7 (and_7_out, comparator_26_eq, comparator_27_eq);
  Comparator #(.width(7)) comparator_28 (
    .a(7'b0000001), .b(Instruction[31:25]), .eq(comparator_28_eq));  // open: gt, lt
  Comparator #(.mode("unsigned"), .width(7)) comparator_29 (
    .a(Instruction[6:0]), .b(7'b0000011), .eq(comparator_29_eq));  // open: gt, lt
  Comparator #(.mode("unsigned"), .width(3)) comparator_30 (
    .a(3'b000), .b(Instruction[14:12]), .eq(comparator_30_eq));  // open: gt, lt
  Comparator #(.mode("unsigned"), .width(3)) comparator_31 (
    .a(3'b001), .b(Instruction[14:12]), .eq(comparator_31_eq));  // open: gt, lt
  Comparator #(.mode("unsigned"), .width(3)) comparator_32 (
    .a(3'b010), .b(Instruction[14:12]), .eq(comparator_32_eq));  // open: gt, lt
  Comparator #(.mode("unsigned"), .width(7)) comparator_33 (
    .a(Instruction[6:0]), .b(7'b0100011), .eq(comparator_33_eq));  // open: gt, lt
  Comparator #(.mode("unsigned"), .width(3)) comparator_34 (
    .a(3'b000), .b(Instruction[14:12]), .eq(comparator_34_eq));  // open: gt, lt
  Comparator #(.mode("unsigned"), .width(3)) comparator_35 (
    .a(3'b001), .b(Instruction[14:12]), .eq(comparator_35_eq));  // open: gt, lt
  Comparator #(.mode("unsigned"), .width(3)) comparator_36 (
    .a(3'b010), .b(Instruction[14:12]), .eq(comparator_36_eq));  // open: gt, lt
  Comparator #(.mode("unsigned"), .width(7)) comparator_37 (
    .a(Instruction[6:0]), .b(7'b0010011), .eq(comparator_37_eq));  // open: gt, lt
  and and_8 (and_8_out, comparator_11_eq, comparator_17_eq);
  and and_9 (and_9_out, comparator_14_eq, comparator_17_eq);
  and and_10 (and_10_out, comparator_14_eq, comparator_18_eq);
  Comparator #(.width(7)) comparator_38 (
    .a(7'b0100000), .b(Instruction[31:25]), .eq(comparator_38_eq));  // open: gt, lt
  and and_11 (and_11_out, comparator_37_eq, comparator_10_eq);
  and and_12 (and_12_out, comparator_37_eq, and_8_out);
  and and_13 (and_13_out, comparator_37_eq, comparator_12_eq);
  and and_14 (and_14_out, comparator_37_eq, comparator_13_eq);
  and and_15 (and_15_out, comparator_37_eq, comparator_15_eq);
  and and_16 (and_16_out, comparator_37_eq, comparator_16_eq);
  and and_17 (and_17_out, comparator_37_eq, and_9_out);
  and and_18 (and_18_out, comparator_37_eq, and_10_out);
  and and_19 (and_19_out, comparator_19_eq, comparator_28_eq);
  and and_20 (and_20_out, comparator_20_eq, comparator_28_eq);
  and and_21 (and_21_out, comparator_22_eq, comparator_28_eq);
  and and_22 (and_22_out, comparator_30_eq, comparator_29_eq);
  and and_23 (and_23_out, comparator_31_eq, comparator_29_eq);
  and and_24 (and_24_out, comparator_32_eq, comparator_29_eq);
  and and_25 (and_25_out, comparator_34_eq, comparator_33_eq);
  and and_26 (and_26_out, comparator_35_eq, comparator_33_eq);
  and and_27 (and_27_out, comparator_36_eq, comparator_33_eq);
  Comparator #(.mode("unsigned"), .width(7)) comparator_39 (
    .a(Instruction[6:0]), .b(7'b0110011), .eq(comparator_39_eq));  // open: gt, lt
  and and_28 (and_28_out, comparator_19_eq, comparator_38_eq);
  and and_29 (and_29_out, comparator_24_eq, comparator_38_eq);
  and and_30 (R_add, and_1_out, comparator_39_eq);
  and and_31 (R_mul, and_19_out, comparator_39_eq);
  and and_32 (R_sub, and_28_out, comparator_39_eq);
  and and_33 (R_sll, and_2_out, comparator_39_eq);
  and and_34 (R_mulh, and_20_out, comparator_39_eq);
  and and_35 (R_slt, and_3_out, comparator_39_eq);
  and and_36 (R_mulhu, and_21_out, comparator_39_eq);
  and and_37 (R_xor, and_4_out, comparator_39_eq);
  and and_38 (R_srl, and_5_out, comparator_39_eq);
  and and_39 (R_sra, and_29_out, comparator_39_eq);
  and and_40 (R_or, and_6_out, comparator_39_eq);
  and and_41 (R_and, and_7_out, comparator_39_eq);
  or or_3 (or_3_out, and_25_out, and_26_out, and_27_out);
  Priority_Encoder priority_encoder_2 (
    .in0(and_11_out), .in1(and_12_out), .in2(and_13_out), .in3(and_18_out), .in4(and_14_out),
    .in5(and_17_out), .in6(and_15_out), .in7(and_16_out), .out(priority_encoder_2_out));  // open: en_in, gs, en_out
  or or_4 (or_4_out, and_22_out, and_23_out, and_24_out);
  assign I_FORMAT = {{3{1'b0}}, priority_encoder_2_out};  // Bit_Extender bit_extender_1
  assign bit_extender_2_out = {{5{1'b0}}, or_4_out};  // Bit_Extender bit_extender_2
  assign bit_extender_3_out = {{5{1'b0}}, or_3_out};  // Bit_Extender bit_extender_3
  Adder #(.width(6)) adder_1 (.a(6'b010110), .b(bit_extender_2_out), .out(LOAD_FORMAT));  // open: cin, cout
  Adder #(.width(6)) adder_2 (.a(6'b010111), .b(bit_extender_3_out), .out(STORE_FORMAT));  // open: cin, cout
  Priority_Encoder #(.select_enc(4)) priority_encoder_3 (
    .in0(R_add), .in1(R_sll), .in2(R_slt), .in3(R_xor), .in4(R_srl), .in5(R_or), .in6(R_and), .in7(R_mul),
    .in8(R_mulh), .in9(R_mulhu), .in10(R_sub), .in11(R_sra), .out(priority_encoder_3_out));  // open: in12, in13, in14, in15, gs, en_out, en_in
  Comparator #(.mode("unsigned"), .width(7)) comparator_40 (
    .a(Instruction[6:0]), .b(7'b1101111), .eq(comparator_40_eq));  // open: gt, lt
  Comparator #(.mode("unsigned"), .width(7)) comparator_41 (
    .a(Instruction[6:0]), .b(7'b1100111), .eq(comparator_41_eq));  // open: gt, lt
  Comparator #(.mode("unsigned"), .width(3)) comparator_42 (
    .a(3'b000), .b(Instruction[14:12]), .eq(comparator_42_eq));  // open: gt, lt
  Comparator #(.mode("unsigned"), .width(7)) comparator_43 (
    .a(Instruction[6:0]), .b(7'b0010111), .eq(comparator_43_eq));  // open: gt, lt
  Comparator #(.mode("unsigned"), .width(7)) comparator_44 (
    .a(Instruction[6:0]), .b(7'b0110111), .eq(comparator_44_eq));  // open: gt, lt
  Comparator #(.width(3)) comparator_45 (.a(3'b000), .b(Instruction[14:12]), .eq(comparator_45_eq));  // open: gt, lt
  Comparator #(.width(3)) comparator_46 (.a(3'b001), .b(Instruction[14:12]), .eq(comparator_46_eq));  // open: gt, lt
  Comparator #(.width(3)) comparator_47 (.a(3'b100), .b(Instruction[14:12]), .eq(comparator_47_eq));  // open: gt, lt
  Comparator #(.width(3)) comparator_48 (.a(3'b101), .b(Instruction[14:12]), .eq(comparator_48_eq));  // open: gt, lt
  Comparator #(.width(3)) comparator_49 (.a(3'b110), .b(Instruction[14:12]), .eq(comparator_49_eq));  // open: gt, lt
  Comparator #(.width(3)) comparator_50 (.a(3'b111), .b(Instruction[14:12]), .eq(comparator_50_eq));  // open: gt, lt
  assign bit_extender_4_out = {{2{1'b0}}, priority_encoder_3_out};  // Bit_Extender bit_extender_4
  Comparator #(.mode("unsigned"), .width(7)) comparator_51 (
    .a(Instruction[6:0]), .b(7'b1101111), .eq(comparator_51_eq));  // open: gt, lt
  Comparator #(.mode("unsigned"), .width(7)) comparator_52 (
    .a(Instruction[6:0]), .b(7'b1100111), .eq(comparator_52_eq));  // open: gt, lt
  Comparator #(.mode("unsigned"), .width(3)) comparator_53 (
    .a(3'b000), .b(Instruction[14:12]), .eq(comparator_53_eq));  // open: gt, lt
  Comparator #(.mode("unsigned"), .width(7)) comparator_54 (
    .a(Instruction[6:0]), .b(7'b1100011), .eq(comparator_54_eq));  // open: gt, lt
  Adder #(.width(6)) adder_3 (.a(6'b001000), .b(bit_extender_4_out), .out(R_FORMAT));  // open: cin, cout
  and and_42 (and_42_out, comparator_41_eq, comparator_42_eq);
  not not_1 (not_1_out, BrEq);
  not not_2 (not_2_out, BrLt);
  not not_3 (not_3_out, BrLt);
  Priority_Encoder #(.select_enc(1)) priority_encoder_4 (
    .in0(comparator_40_eq), .in1(and_42_out), .out(priority_encoder_4_out));  // open: gs, en_out, en_in
  Priority_Encoder #(.select_enc(1)) priority_encoder_5 (
    .in0(comparator_43_eq), .in1(comparator_44_eq), .out(priority_encoder_5_out));  // open: gs, en_out, en_in
  and and_43 (and_43_out, B_beq, BrEq);
  and and_44 (and_44_out, B_bne, not_1_out);
  and and_45 (and_45_out, B_blt, BrLt);
  and and_46 (and_46_out, B_bge, not_2_out);
  and and_47 (and_47_out, B_bltu, BrLt);
  and and_48 (and_48_out, B_bgeu, not_3_out);
  and and_49 (and_49_out, comparator_52_eq, comparator_53_eq);
  and and_50 (B_beq, comparator_45_eq, comparator_54_eq);
  and and_51 (B_bne, comparator_46_eq, comparator_54_eq);
  and and_52 (B_blt, comparator_47_eq, comparator_54_eq);
  and and_53 (B_bge, comparator_48_eq, comparator_54_eq);
  and and_54 (B_bltu, comparator_49_eq, comparator_54_eq);
  and and_55 (B_bgeu, comparator_50_eq, comparator_54_eq);
  assign bit_extender_5_out = {{5{1'b0}}, priority_encoder_4_out};  // Bit_Extender bit_extender_5
  assign bit_extender_6_out = {{5{1'b0}}, priority_encoder_5_out};  // Bit_Extender bit_extender_6
  or or_5 (or_5_out, and_43_out, and_44_out, and_45_out, and_46_out, and_47_out, and_48_out);
  or or_6 (or_6_out, comparator_51_eq, and_49_out);
  Adder #(.width(6)) adder_4 (.a(6'b011000), .b(bit_extender_5_out), .out(Jump));  // open: cin, cout
  Adder #(.width(6)) adder_5 (.a(6'b011010), .b(bit_extender_6_out), .out(U_FORMAT));  // open: cin, cout
  or or_7 (or_7_out, B_beq, B_bne, B_blt, B_bge);
  or or_8 (or_8_out, B_bltu, B_bgeu);
  or or_9 (PCSel, or_5_out, or_6_out);
  Priority_Encoder #(.select_enc(1)) priority_encoder_6 (
    .in0(or_7_out), .in1(or_8_out), .out(priority_encoder_6_out));  // open: gs, en_out, en_in
  assign bit_extender_7_out = {{5{1'b0}}, priority_encoder_6_out};  // Bit_Extender bit_extender_7
  Adder #(.width(6)) adder_6 (.a(6'b010100), .b(bit_extender_7_out), .out(B_FORMAT));  // open: cin, cout

  // Other names for the same wires on the sheet: Opcode[6:0] = Instruction[6:0]; rd[4:0] = Instruction[11:7];
  //   funct3[2:0] = Instruction[14:12]; rs1[4:0] = Instruction[19:15]; rs2[4:0] = Instruction[24:20];
  //   funct7[6:0] = Instruction[31:25]

  // Notes on the sheet:
  //   INPUTS to your circuit
  //   contents of rom_1 (hex, n*v repeats v):
  //   1041 10c1 1141 16c1 1241 12c1 1341 13c1 1001 1081 1101 1201 1281 1301 1381 1401 1481 1581 1601 1681
  //   1064 1074 41 1842 2069 2041 1047 3047
  //   ROM FOR CONTROL LOGIC
  //   DON'T CHANGE THE LOCATIONS OF THE INPUTS AND OUTPUTS!
  //   This is only if you choose to do the ROM option
  //   CONNECT
  //   WIRE
  //   TO
  //   USE
  //   ROM
  //   OUTPUT from your circuit
  //   Reminder: If using ROM, use combinational logic for PCSel
endmodule
