// Logisim project cpu.circ as structural Verilog: 1 circuit, main circuit cpu
module cpu (
  input  clk,
  input  [31:0] Instruction,
  input  [31:0] MemReadData,
  output [31:0] MemAddress,
  output [31:0] ProgramCounter,
  output [31:0] ra,
  output [31:0] sp,
  output [31:0] t0,
  output [31:0] t1,
  output [31:0] t2,
  output [31:0] s0,
  output [31:0] s1,
  output [31:0] a0,
  output [3:0] MemWriteMask,
  output [31:0] MemWriteData
);

  wire BrEq, BrLt, BrUn, control_logic_1_asel, control_logic_1_bsel, control_logic_1_regwen, MemWEn, PCSel;
  wire [1:0] control_logic_1_wbsel;
  wire [2:0] control_logic_1_immsel, funct3;
  wire [3:0] control_logic_1_alusel;
  wire [4:0] immI;
  wire [6:0] funct7;
  wire [19:0] Instruction2;
  wire [31:0] DataToReg, imm_gen_1_immediate, multiplexer_1_out, multiplexer_2_out, multiplexer_3_out,
       multiplexer_4_out, multiplexer_5_out, nextPC, regfile_1_readdata1, regfile_1_readdata2, register_1_q,
       register_2_q;

  Adder #(.width(32)) adder_1 (.a(ProgramCounter), .b(32'h4), .out(nextPC));  // open: cin, cout
  Register #(.width(32)) PC (.D(multiplexer_1_out), .en(1'b1), .clk(clk), .Q(ProgramCounter));  // open: clr
  Multiplexer #(.width(32)) multiplexer_1 (.in0(nextPC), .in1(MemAddress), .out(multiplexer_1_out), .sel(PCSel));
  control_logic control_logic_1 (
    .Instruction({funct7, immI, Instruction2[19:15], funct3, Instruction2[11:0]}), .BrEq(BrEq), .BrLt(BrLt),
    .PCSel(PCSel), .RegWEn(control_logic_1_regwen), .ImmSel(control_logic_1_immsel), .BrUn(BrUn),
    .ASel(control_logic_1_asel), .BSel(control_logic_1_bsel), .ALUSel(control_logic_1_alusel),
    .MemWEn(MemWEn), .WBSel(control_logic_1_wbsel));
  Register #(.width(32)) register_1 (.D(ProgramCounter), .en(1'b1), .clk(clk), .Q(register_1_q));  // open: clr
  regfile regfile_1 (
    .ReadIndex1(Instruction2[19:15]), .ReadIndex2(immI), .WriteIndex(Instruction2[11:7]),
    .WriteData(multiplexer_2_out), .RegWEn(control_logic_1_regwen), .clk(clk), .ra(ra), .sp(sp), .t0(t0),
    .t1(t1), .t2(t2), .s0(s0), .s1(s1), .a0(a0), .ReadData1(regfile_1_readdata1),
    .ReadData2(regfile_1_readdata2));
  Multiplexer #(.select(2), .width(32)) multiplexer_2 (
    .in0(DataToReg), .in1(MemAddress), .in2(register_2_q), .in3(imm_gen_1_immediate),
    .out(multiplexer_2_out), .sel(control_logic_1_wbsel));
  imm_gen imm_gen_1 (
    .Instruction({funct7, immI, Instruction2[19:15], funct3, Instruction2[11:0]}),
    .ImmSel(control_logic_1_immsel), .Immediate(imm_gen_1_immediate));
  Multiplexer #(.width(32)) multiplexer_3 (
    .in0(regfile_1_readdata1), .in1(register_1_q), .out(multiplexer_3_out), .sel(control_logic_1_asel));
  Multiplexer #(.width(32)) multiplexer_4 (
    .in0(regfile_1_readdata2), .in1(imm_gen_1_immediate), .out(multiplexer_4_out), .sel(control_logic_1_bsel));
  alu alu_1 (.A(multiplexer_3_out), .B(multiplexer_4_out), .ALUSel(control_logic_1_alusel), .ALUResult(MemAddress));
  branch_comp branch_comp_1 (
    .BrData1(regfile_1_readdata1), .BrData2(regfile_1_readdata2), .BrUn(BrUn), .BrEq(BrEq), .BrLt(BrLt));
  Register #(.width(32)) register_2 (.D(nextPC), .en(1'b1), .clk(clk), .Q(register_2_q));  // open: clr
  partial_load partial_load_1 (
    .Instruction({funct7, immI, Instruction2[19:15], funct3, Instruction2[11:0]}), .MemAddress(MemAddress),
    .DataFromMem(MemReadData), .DataToReg(DataToReg));
  partial_store partial_store_1 (
    .Instruction({funct7, immI, Instruction2[19:15], funct3, Instruction2[11:0]}), .MemAddress(MemAddress),
    .DataFromReg(regfile_1_readdata2), .MemWEn(MemWEn), .MemWriteMask(MemWriteMask), .DataToMem(MemWriteData));
  Multiplexer #(.width(32)) multiplexer_5 (.in0(Instruction), .in1(32'h13), .out(multiplexer_5_out), .sel(PCSel));
  Register #(.width(32)) register_3 (
    .D(multiplexer_5_out), .en(1'b1), .clk(clk),
    .Q({funct7, immI, Instruction2[19:15], funct3, Instruction2[11:0]}));  // open: clr

  // Other names for the same wires on the sheet: ALUResult[31:0] = MemAddress; Opcode[6:0] = Instruction2[6:0];
  //   rd[4:0] = Instruction2[11:7]; Instruction2 (some bits) = {funct7, immI, funct3}; rs1[4:0] = Instruction2[19:15];
  //   rs2[4:0] = immI; immI[11:5] = funct7

  // Notes on the sheet:
  //   To IMEM
  //   IMEM (do **NOT** move this)
  //   From IMEM
  //   Inputs/Outputs for testing. Do **NOT** move these.
  //   It is OK to move the PC, RegFile, ALU, MEM, Branch Comp, Imm Gen, Partial Load, Partial Store and Control Logic to wherever is most convenient for you when constructing your CPU, and to delete this text
  //   To DMEM
  //   DMEM (do **NOT** move this)
  //   From DMEM
endmodule
