// Logisim project imm-gen.circ as structural Verilog: 1 circuit, main circuit imm_gen
module imm_gen (
  input  [31:0] Instruction,
  input  [2:0] ImmSel,
  output [31:0] Immediate
);

  wire [31:0] B_imm, bit_extender_1_out, bit_extender_2_out, bit_extender_3_out, bit_extender_4_out, I_imm,
       J_imm, S_imm, U_imm;

  Demultiplexer #(.select(3), .width(32)) demultiplexer_1 (
    .out0(I_imm), .out1(S_imm), .out2(B_imm), .out3(U_imm), .out4(J_imm), .in(Instruction), .sel(ImmSel));  // open: out5, out6, out7
  assign bit_extender_1_out = {{20{I_imm[31]}}, I_imm[31:20]};  // Bit_Extender bit_extender_1
  assign bit_extender_2_out = {{20{S_imm[31]}}, {S_imm[31:25], S_imm[11:7]}};  // Bit_Extender bit_extender_2
  assign bit_extender_3_out = {{19{B_imm[31]}}, {B_imm[31], B_imm[7], B_imm[30:25], B_imm[11:8], 1'b0}};  // Bit_Extender bit_extender_3
  assign bit_extender_4_out = {{11{J_imm[31]}}, {J_imm[31], J_imm[19:12], J_imm[20], J_imm[30:21], 1'b0}};  // Bit_Extender bit_extender_4
  Multiplexer #(.select(3), .width(32)) multiplexer_1 (
    .in0(bit_extender_1_out), .in1(bit_extender_2_out), .in2(bit_extender_3_out),
    .in3({U_imm[31:12], {12{1'b0}}}), .in4(bit_extender_4_out), .out(Immediate), .sel(ImmSel));  // open: in5, in6, in7

  // Notes on the sheet:
  //   INPUTS to your circuit
  //   DON'T CHANGE THE LOCATIONS OF THE INPUTS AND OUTPUTS!
  //   OUTPUT from your circuit
endmodule
