// Logisim project partial-load.circ as structural Verilog: 1 circuit, main circuit partial_load
module partial_load (
  input  [31:0] Instruction,
  input  [31:0] MemAddress,
  input  [31:0] DataFromMem,
  output [31:0] DataToReg
);

  wire and_4_out, and_5_out, and_6_out, and_7_out, and_8_out, and_9_out, and_10_out, and_11_out,
       comparator_1_eq, comparator_2_eq, comparator_3_eq, comparator_4_eq, comparator_5_eq, comparator_6_eq,
       comparator_7_eq, comparator_8_eq, comparator_9_eq, comparator_10_eq, comparator_11_eq,
       comparator_12_eq, lb, lh, lw;
  wire [2:0] Sel;
  wire [31:0] bit_extender_1_out, bit_extender_2_out, bit_extender_3_out, bit_extender_4_out,
       bit_extender_5_out, bit_extender_6_out, bit_extender_7_out;

  Comparator #(.mode("unsigned"), .width(7)) comparator_1 (
    .a(Instruction[6:0]), .b(7'b0000011), .eq(comparator_1_eq));  // open: gt, lt
  Comparator #(.mode("unsigned"), .width(3)) comparator_2 (
    .a(3'b000), .b(Instruction[14:12]), .eq(comparator_2_eq));  // open: gt, lt
  Comparator #(.mode("unsigned"), .width(3)) comparator_3 (
    .a(3'b001), .b(Instruction[14:12]), .eq(comparator_3_eq));  // open: gt, lt
  Comparator #(.mode("unsigned"), .width(3)) comparator_4 (
    .a(3'b010), .b(Instruction[14:12]), .eq(comparator_4_eq));  // open: gt, lt
  assign bit_extender_1_out = {{24{DataFromMem[7]}}, DataFromMem[7:0]};  // Bit_Extender bit_extender_1
  assign bit_extender_2_out = {{24{DataFromMem[15]}}, DataFromMem[15:8]};  // Bit_Extender bit_extender_2
  assign bit_extender_3_out = {{24{DataFromMem[23]}}, DataFromMem[23:16]};  // Bit_Extender bit_extender_3
  assign bit_extender_4_out = {{24{DataFromMem[31]}}, DataFromMem[31:24]};  // Bit_Extender bit_extender_4
  assign bit_extender_5_out = {{16{DataFromMem[15]}}, DataFromMem[15:0]};  // Bit_Extender bit_extender_5
  assign bit_extender_6_out = {{16{DataFromMem[23]}}, DataFromMem[23:8]};  // Bit_Extender bit_extender_6
  assign bit_extender_7_out = {{16{DataFromMem[31]}}, DataFromMem[31:16]};  // Bit_Extender bit_extender_7
  and and_1 (lb, comparator_2_eq, comparator_1_eq);
  and and_2 (lh, comparator_3_eq, comparator_1_eq);
  and and_3 (lw, comparator_4_eq, comparator_1_eq);
  Multiplexer #(.select(3), .width(32)) multiplexer_1 (
    .in0(bit_extender_1_out), .in1(bit_extender_2_out), .in2(bit_extender_3_out), .in3(bit_extender_4_out),
    .in4(bit_extender_5_out), .in5(bit_extender_6_out), .in6(bit_extender_7_out), .in7(DataFromMem),
    .out(DataToReg), .sel(Sel));
  Comparator #(.mode("unsigned"), .width(2)) comparator_5 (
    .a(2'b00), .b(MemAddress[1:0]), .eq(comparator_5_eq));  // open: gt, lt
  Comparator #(.mode("unsigned"), .width(2)) comparator_6 (
    .a(2'b01), .b(MemAddress[1:0]), .eq(comparator_6_eq));  // open: gt, lt
  Comparator #(.mode("unsigned"), .width(2)) comparator_7 (
    .a(2'b10), .b(MemAddress[1:0]), .eq(comparator_7_eq));  // open: gt, lt
  Comparator #(.mode("unsigned"), .width(2)) comparator_8 (
    .a(2'b11), .b(MemAddress[1:0]), .eq(comparator_8_eq));  // open: gt, lt
  Comparator #(.mode("unsigned"), .width(2)) comparator_9 (
    .a(2'b00), .b(MemAddress[1:0]), .eq(comparator_9_eq));  // open: gt, lt
  Comparator #(.mode("unsigned"), .width(2)) comparator_10 (
    .a(2'b01), .b(MemAddress[1:0]), .eq(comparator_10_eq));  // open: gt, lt
  Comparator #(.mode("unsigned"), .width(2)) comparator_11 (
    .a(2'b10), .b(MemAddress[1:0]), .eq(comparator_11_eq));  // open: gt, lt
  Comparator #(.mode("unsigned"), .width(2)) comparator_12 (
    .a(2'b00), .b(MemAddress[1:0]), .eq(comparator_12_eq));  // open: gt, lt
  and and_4 (and_4_out, lb, comparator_5_eq);
  and and_5 (and_5_out, lb, comparator_6_eq);
  and and_6 (and_6_out, lb, comparator_7_eq);
  and and_7 (and_7_out, lb, comparator_8_eq);
  and and_8 (and_8_out, lh, comparator_9_eq);
  and and_9 (and_9_out, lh, comparator_10_eq);
  and and_10 (and_10_out, lh, comparator_11_eq);
  and and_11 (and_11_out, lw, comparator_12_eq);
  Priority_Encoder priority_encoder_1 (
    .in0(and_4_out), .in1(and_5_out), .in2(and_6_out), .in3(and_7_out), .in4(and_8_out), .in5(and_9_out),
    .in6(and_10_out), .in7(and_11_out), .out(Sel));  // open: en_in, gs, en_out

  // Other names for the same wires on the sheet: Opcode[6:0] = Instruction[6:0]; rd[4:0] = Instruction[11:7];
  //   funct3[2:0] = Instruction[14:12]; rs1[4:0] = Instruction[19:15]; rs2[4:0] = Instruction[24:20];
  //   funct7[6:0] = Instruction[31:25]; Least2Bits[1:0] = MemAddress[1:0]

  // Notes on the sheet:
  //   INPUTS to your circuit
  //   DON'T CHANGE THE LOCATIONS OF THE INPUTS AND OUTPUTS!
  //   OUTPUT from your circuit
endmodule
