// Logisim project partial-store.circ as structural Verilog: 1 circuit, main circuit partial_store
module partial_store (
  input  [31:0] Instruction,
  input  [31:0] MemAddress,
  input  [31:0] DataFromReg,
  input  MemWEn,
  output [3:0] MemWriteMask,
  output [31:0] DataToMem
);

  wire and_4_out, and_5_out, and_6_out, and_7_out, and_8_out, and_9_out, and_10_out, comparator_1_eq,
       comparator_2_eq, comparator_3_eq, comparator_4_eq, comparator_5_eq, comparator_6_eq, comparator_7_eq,
       comparator_8_eq, comparator_9_eq, comparator_10_eq, comparator_11_eq, sb, sh, sw;
  wire [2:0] Sel;
  wire [3:0] multiplexer_3_out;
  wire [31:0] bit_extender_1_out, bit_extender_2_out, multiplexer_1_out, shifter_1_out, shifter_2_out,
       shifter_3_out, shifter_4_out;

  assign bit_extender_1_out = {{24{1'b0}}, DataFromReg[7:0]};  // Bit_Extender bit_extender_1
  assign bit_extender_2_out = {{16{1'b0}}, DataFromReg[15:0]};  // Bit_Extender bit_extender_2
  Comparator #(.mode("unsigned"), .width(7)) comparator_1 (
    .a(Instruction[6:0]), .b(7'b0100011), .eq(comparator_1_eq));  // open: gt, lt
  Comparator #(.mode("unsigned"), .width(3)) comparator_2 (
    .a(3'b000), .b(Instruction[14:12]), .eq(comparator_2_eq));  // open: gt, lt
  Comparator #(.mode("unsigned"), .width(3)) comparator_3 (
    .a(3'b001), .b(Instruction[14:12]), .eq(comparator_3_eq));  // open: gt, lt
  Comparator #(.mode("unsigned"), .width(3)) comparator_4 (
    .a(3'b010), .b(Instruction[14:12]), .eq(comparator_4_eq));  // open: gt, lt
  Shifter #(.width(32)) shifter_1 (.in(bit_extender_1_out), .\dist (5'b01000), .out(shifter_1_out));
  Shifter #(.width(32)) shifter_2 (.in(bit_extender_1_out), .\dist (5'b10000), .out(shifter_2_out));
  Shifter #(.width(32)) shifter_3 (.in(bit_extender_1_out), .\dist (5'b11000), .out(shifter_3_out));
  Shifter #(.width(32)) shifter_4 (.in(bit_extender_2_out), .\dist (5'b10000), .out(shifter_4_out));
  and and_1 (sb, comparator_2_eq, comparator_1_eq);
  and and_2 (sh, comparator_3_eq, comparator_1_eq);
  and and_3 (sw, comparator_4_eq, comparator_1_eq);
  Multiplexer #(.select(3), .width(32)) multiplexer_1 (
    .in0(bit_extender_1_out), .in1(shifter_1_out), .in2(shifter_2_out), .in3(shifter_3_out),
    .in4(bit_extender_2_out), .in5(shifter_4_out), .in6(DataFromReg), .out(multiplexer_1_out), .sel(Sel));  // open: in7
  Multiplexer #(.width(32)) multiplexer_2 (.in0({32{1'b0}}), .in1(multiplexer_1_out), .out(DataToMem), .sel(MemWEn));
  Comparator #(.mode("unsigned"), .width(2)) comparator_5 (
    .a(2'b00), .b(MemAddress[1:0]), .eq(comparator_5_eq));  // open: gt, lt
  Comparator #(.mode("unsigned"), .width(2)) comparator_6 (
    .a(2'b01), .b(MemAddress[1:0]), .eq(comparator_6_eq));  // open: gt, lt
  Comparator #(.mode("unsigned"), .width(2)) comparator_7 (
    .a(2'b10), .b(MemAddress[1:0]), .eq(comparator_7_eq));  // open: gt, lt
  Comparator #(.mode("unsigned"), .width(2)) comparator_8 (
    .a(2'b11), .b(MemAddress[1:0]), .eq(comparator_8_eq));  // open: gt, lt
  Comparator #(.mode("unsigned"), .width(2)) comparator_9 (
    .a(2'b00), .b(MemAddress[1:0]), .eq(comparator_9_eq));  // open: gt, lt
  Comparator #(.mode("unsigned"), .width(2)) comparator_10 (
    .a(2'b10), .b(MemAddress[1:0]), .eq(comparator_10_eq));  // open: gt, lt
  Comparator #(.mode("unsigned"), .width(2)) comparator_11 (
    .a(2'b00), .b(MemAddress[1:0]), .eq(comparator_11_eq));  // open: gt, lt
  and and_4 (and_4_out, sb, comparator_5_eq);
  and and_5 (and_5_out, sb, comparator_6_eq);
  and and_6 (and_6_out, sb, comparator_7_eq);
  and and_7 (and_7_out, sb, comparator_8_eq);
  and and_8 (and_8_out, sh, comparator_9_eq);
  and and_9 (and_9_out, sh, comparator_10_eq);
  and and_10 (and_10_out, sw, comparator_11_eq);
  Priority_Encoder priority_encoder_1 (
    .in0(and_4_out), .in1(and_5_out), .in2(and_6_out), .in3(and_7_out), .in4(and_8_out), .in5(and_9_out),
    .in6(and_10_out), .out(Sel));  // open: in7, en_in, gs, en_out
  Multiplexer #(.select(3), .width(4)) multiplexer_3 (
    .in0(4'b0001), .in1(4'b0010), .in2(4'b0100), .in3(4'b1000), .in4(4'b0011), .in5(4'b1100), .in6(4'b1111),
    .out(multiplexer_3_out), .sel(Sel));  // open: in7
  Multiplexer #(.width(4)) multiplexer_4 (.in0(4'b0000), .in1(multiplexer_3_out), .out(MemWriteMask), .sel(MemWEn));

  // Other names for the same wires on the sheet: Opcode[6:0] = Instruction[6:0]; rd[4:0] = Instruction[11:7];
  //   funct3[2:0] = Instruction[14:12]; rs1[4:0] = Instruction[19:15]; rs2[4:0] = Instruction[24:20];
  //   funct7[6:0] = Instruction[31:25]; Least2Bits[1:0] = MemAddress[1:0]

  // Notes on the sheet:
  //   INPUTS to your circuit
  //   DON'T CHANGE THE LOCATIONS OF THE INPUTS AND OUTPUTS!
  //   OUTPUT from your circuit
endmodule
