// Logisim project regfile.circ as structural Verilog: 1 circuit, main circuit regfile
module regfile (
  input  [4:0] ReadIndex1,
  input  [4:0] ReadIndex2,
  input  [4:0] WriteIndex,
  input  [31:0] WriteData,
  input  RegWEn,
  input  clk,
  output [31:0] ra,
  output [31:0] sp,
  output [31:0] t0,
  output [31:0] t1,
  output [31:0] t2,
  output [31:0] s0,
  output [31:0] s1,
  output [31:0] a0,
  output [31:0] ReadData1,
  output [31:0] ReadData2
);

  wire demultiplexer_1_out1, demultiplexer_1_out2, demultiplexer_1_out4, demultiplexer_1_out5,
       demultiplexer_1_out6, demultiplexer_1_out7, demultiplexer_1_out8, demultiplexer_1_out9,
       demultiplexer_1_out10, demultiplexer_1_out12, demultiplexer_1_out20, demultiplexer_1_out31, e3, e11,
       e13, e14, e15, e16, e17, e18, e19, e20, e21, e22, e23, e24, e25, e26, e27, e28, e29, e30;
  wire [31:0] a1, a2, a3, a4, a5, a6, a7, D3, D11, D13, D14, D15, D16, D17, D18, D19, D20, D21, D22, D23,
       D24, D25, D26, D27, D28, D29, D30, demultiplexer_2_out1, demultiplexer_2_out2, demultiplexer_2_out4,
       demultiplexer_2_out5, demultiplexer_2_out6, demultiplexer_2_out7, demultiplexer_2_out8,
       demultiplexer_2_out9, demultiplexer_2_out10, demultiplexer_2_out12, demultiplexer_2_out20,
       demultiplexer_2_out31, gp, s2, s3, s4, s5, s6, s7, s8, s9, s10, s11, t3, t4, t5, t6, tp;

  Demultiplexer #(.select(5)) demultiplexer_1 (
    .out1(demultiplexer_1_out1), .out2(demultiplexer_1_out2), .out3(e3), .out4(demultiplexer_1_out4),
    .out5(demultiplexer_1_out5), .out6(demultiplexer_1_out6), .out7(demultiplexer_1_out7),
    .out8(demultiplexer_1_out8), .out9(demultiplexer_1_out9), .out10(demultiplexer_1_out10), .out11(e11),
    .out12(demultiplexer_1_out12), .out13(e13), .out14(e14), .out15(e15), .out16(e16), .out17(e17),
    .out18(e18), .out19(e19), .out20(demultiplexer_1_out20), .out21(e21), .out22(e22), .out23(e23),
    .out24(e24), .out25(e25), .out26(e26), .out27(e27), .out28(e28), .out29(e29), .out30(e30),
    .out31(demultiplexer_1_out31), .in(RegWEn), .sel(WriteIndex));  // open: out0
  Demultiplexer #(.select(5), .width(32)) demultiplexer_2 (
    .out1(demultiplexer_2_out1), .out2(demultiplexer_2_out2), .out3(D3), .out4(demultiplexer_2_out4),
    .out5(demultiplexer_2_out5), .out6(demultiplexer_2_out6), .out7(demultiplexer_2_out7),
    .out8(demultiplexer_2_out8), .out9(demultiplexer_2_out9), .out10(demultiplexer_2_out10), .out11(D11),
    .out12(demultiplexer_2_out12), .out13(D13), .out14(D14), .out15(D15), .out16(D16), .out17(D17),
    .out18(D18), .out19(D19), .out20(demultiplexer_2_out20), .out21(D21), .out22(D22), .out23(D23),
    .out24(D24), .out25(D25), .out26(D26), .out27(D27), .out28(D28), .out29(D29), .out30(D30),
    .out31(demultiplexer_2_out31), .in(WriteData), .sel(WriteIndex));  // open: out0
  Register #(.width(32)) register_1 (
    .D(demultiplexer_2_out1), .en(demultiplexer_1_out1), .clk(clk), .Q(ra));  // open: clr
  Register #(.width(32)) register_2 (
    .D(demultiplexer_2_out2), .en(demultiplexer_1_out2), .clk(clk), .Q(sp));  // open: clr
  Register #(.width(32)) register_3 (
    .D(demultiplexer_2_out5), .en(demultiplexer_1_out5), .clk(clk), .Q(t0));  // open: clr
  Register #(.width(32)) register_4 (
    .D(demultiplexer_2_out6), .en(demultiplexer_1_out6), .clk(clk), .Q(t1));  // open: clr
  Register #(.width(32)) register_5 (
    .D(demultiplexer_2_out7), .en(demultiplexer_1_out7), .clk(clk), .Q(t2));  // open: clr
  Register #(.width(32)) register_6 (
    .D(demultiplexer_2_out8), .en(demultiplexer_1_out8), .clk(clk), .Q(s0));  // open: clr
  Register #(.width(32)) register_7 (
    .D(demultiplexer_2_out9), .en(demultiplexer_1_out9), .clk(clk), .Q(s1));  // open: clr
  Register #(.width(32)) register_8 (
    .D(demultiplexer_2_out10), .en(demultiplexer_1_out10), .clk(clk), .Q(a0));  // open: clr
  Register #(.width(32)) register_9 (
    .D(demultiplexer_2_out4), .en(demultiplexer_1_out4), .clk(clk), .Q(tp));  // open: clr
  Register #(.width(32)) register_10 (
    .D(demultiplexer_2_out12), .en(demultiplexer_1_out12), .clk(clk), .Q(a2));  // open: clr
  Register #(.width(32)) register_11 (
    .D(demultiplexer_2_out20), .en(demultiplexer_1_out20), .clk(clk), .Q(s4));  // open: clr
  Register #(.width(32)) register_12 (
    .D(demultiplexer_2_out31), .en(demultiplexer_1_out31), .clk(clk), .Q(t6));  // open: clr
  Multiplexer #(.select(5), .width(32)) multiplexer_1 (
    .in0({32{1'b0}}), .in1(ra), .in2(sp), .in3(gp), .in4(tp), .in5(t0), .in6(t1), .in7(t2), .in8(s0),
    .in9(s1), .in10(a0), .in11(a1), .in12(a2), .in13(a3), .in14(a4), .in15(a5), .in16(a6), .in17(a7),
    .in18(s2), .in19(s3), .in20(s4), .in21(s5), .in22(s6), .in23(s7), .in24(s8), .in25(s9), .in26(s10),
    .in27(s11), .in28(t3), .in29(t4), .in30(t5), .in31(t6), .out(ReadData1), .sel(ReadIndex1));
  Register #(.width(32)) register_13 (.D(D3), .en(e3), .clk(clk), .Q(gp));  // open: clr
  Register #(.width(32)) register_14 (.D(D11), .en(e11), .clk(clk), .Q(a1));  // open: clr
  Register #(.width(32)) register_15 (.D(D13), .en(e13), .clk(clk), .Q(a3));  // open: clr
  Register #(.width(32)) register_16 (.D(D14), .en(e14), .clk(clk), .Q(a4));  // open: clr
  Register #(.width(32)) register_17 (.D(D15), .en(e15), .clk(clk), .Q(a5));  // open: clr
  Register #(.width(32)) register_18 (.D(D16), .en(e16), .clk(clk), .Q(a6));  // open: clr
  Register #(.width(32)) register_19 (.D(D17), .en(e17), .clk(clk), .Q(a7));  // open: clr
  Register #(.width(32)) register_20 (.D(D18), .en(e18), .clk(clk), .Q(s2));  // open: clr
  Register #(.width(32)) register_21 (.D(D19), .en(e19), .clk(clk), .Q(s3));  // open: clr
  Register #(.width(32)) register_22 (.D(D21), .en(e21), .clk(clk), .Q(s5));  // open: clr
  Register #(.width(32)) register_23 (.D(D22), .en(e22), .clk(clk), .Q(s6));  // open: clr
  Register #(.width(32)) register_24 (.D(D23), .en(e23), .clk(clk), .Q(s7));  // open: clr
  Register #(.width(32)) register_25 (.D(D24), .en(e24), .clk(clk), .Q(s8));  // open: clr
  Register #(.width(32)) register_26 (.D(D25), .en(e25), .clk(clk), .Q(s9));  // open: clr
  Register #(.width(32)) register_27 (.D(D26), .en(e26), .clk(clk), .Q(s10));  // open: clr
  Register #(.width(32)) register_28 (.D(D27), .en(e27), .clk(clk), .Q(s11));  // open: clr
  Register #(.width(32)) register_29 (.D(D28), .en(e28), .clk(clk), .Q(t3));  // open: clr
  Register #(.width(32)) register_30 (.D(D29), .en(e29), .clk(clk), .Q(t4));  // open: clr
  Register #(.width(32)) register_31 (.D(D30), .en(e30), .clk(clk), .Q(t5));  // open: clr
  Register #(.width(32)) register_32 (.D(D20), .en(e20), .clk(clk), .Q(s4));  // open: clr
  Multiplexer #(.select(5), .width(32)) multiplexer_2 (
    .in0({32{1'b0}}), .in1(ra), .in2(sp), .in3(gp), .in4(tp), .in5(t0), .in6(t1), .in7(t2), .in8(s0),
    .in9(s1), .in10(a0), .in11(a1), .in12(a2), .in13(a3), .in14(a4), .in15(a5), .in16(a6), .in17(a7),
    .in18(s2), .in19(s3), .in20(s4), .in21(s5), .in22(s6), .in23(s7), .in24(s8), .in25(s9), .in26(s10),
    .in27(s11), .in28(t3), .in29(t4), .in30(t5), .in31(t6), .out(ReadData2), .sel(ReadIndex2));

  // Notes on the sheet:
  //   INPUTS to your circuit
  //   DON'T CHANGE THE LOCATIONS OF THE INPUTS AND OUTPUTS!
  //   These are DEBUG/TEST outputs from your circuit.
  //   OUTPUTS from your circuit
endmodule
